# Fritzing sketch 模拟温度 (saved by Fritzing 0.8.7b)
breadboards: 1

parts:
  R4 = Rotary Potentiometer (Small) [maximum_resistance=100kΩ package=THT]
  R5 = Resistor [tolerance=±5% resistance=10k package=THT]
  元件1 = Arduino Uno (Rev3) - ICSP
  U1 = LCD-16X2 [package=lcd-16x2]
  C1 = Ceramic Capacitor [capacitance=100nF package="100 mil [THT, multilayer]"]

nets:
  N1: R4.wiper, U1.VO
  GND: R4.leg2, R5.Pin_0, 元件1.GND, U1.VSS, U1.R_W, U1.K
  N2: R5.Pin_1, 元件1.A0, C1.1
  N3: 元件1.ICSP_MISO, 元件1.D12/MISO, U1.DB6
  N4: 元件1.ICSP_MOSI, 元件1.D11_PWM/MOSI, U1.DB5
  N5: 元件1.D10_PWM/SS, U1.DB4
  N6: 元件1.D13/SCK, U1.DB7
  N7: 元件1.D4, U1.RS
  N8: 元件1.D5_PWM, U1.E
  N9: 元件1.3V3, U1.A
  5V: 元件1.5V, U1.VDD, C1.0
