# Fritzing sketch Voltmeter (saved by Fritzing 0.8.7b)
breadboards: 1

parts:
  LCD1602 = LCD screen
  R1 = Rotary Potentiometer (Small) [maximum_resistance=100kΩ package=THT]
  R2 = Rotary Potentiometer (Small) [maximum_resistance=100kΩ package=THT]
  元件1 = Arduino Uno (Rev3) - ICSP

nets:
  VSS: LCD1602.VSS, LCD1602.R/W, LCD1602.LED-, R1.leg2, R2.leg1, 元件1.GND
  VDD: LCD1602.VDD, R2.leg2, 元件1.5V
  N1: LCD1602.V0, R1.wiper
  N2: LCD1602.RS, 元件1.D4
  N3: LCD1602.E, 元件1.D6_PWM
  N4: LCD1602.DB4, 元件1.D10_PWM/SS
  N5: LCD1602.DB5, 元件1.D11_PWM/MOSI
  N6: LCD1602.DB6, 元件1.ICSP_MISO, 元件1.D12/MISO
  N7: LCD1602.DB7, 元件1.D13/SCK
  N8: LCD1602.LED+, 元件1.3V3
  N9: R2.wiper, 元件1.A0
