# Fritzing sketch stopwatah (saved by Fritzing 0.8.7b)
breadboards: 1

parts:
  元件1 = Arduino Uno (Rev3) - ICSP
  LED1 = 7-SEGMENT-4DIGIT-YOUNGSUN [package=7-segment-4digit-youngsun-longpads]
  R1 = Resistor [tolerance=±5% resistance=220 package=THT]
  R2 = Resistor [tolerance=±5% resistance=220 package=THT]
  R3 = Resistor [tolerance=±5% resistance=220 package=THT]
  R4 = Resistor [tolerance=±5% resistance=220 package=THT]
  R5 = Resistor [tolerance=±5% resistance=220 package=THT]
  R6 = Resistor [tolerance=±5% resistance=220 package=THT]
  R7 = Resistor [tolerance=±5% resistance=220 package=THT]
  R8 = Resistor [tolerance=±5% resistance=220 package=THT]

nets:
  N1: 元件1.ICSP_MISO, 元件1.D12/MISO, LED1.COL-C
  N2: 元件1.ICSP_MOSI, 元件1.D11_PWM/MOSI, LED1.F
  N3: 元件1.D8, R8.Pin_1
  N4: 元件1.D9_PWM, R7.Pin_1
  N5: 元件1.D10_PWM/SS, LED1.DP
  N6: 元件1.D13/SCK, LED1.G
  N7: 元件1.D2, R3.Pin_0
  N8: 元件1.D3_PWM, R1.Pin_1
  N9: 元件1.D4, R6.Pin_1
  N10: 元件1.D5_PWM, R5.Pin_0
  N11: 元件1.D6_PWM, R4.Pin_0
  N12: 元件1.D7, R2.Pin_0
  N13: LED1.DIG2, R4.Pin_1
  N14: LED1.D, R5.Pin_1
  N15: LED1.COL-A, R7.Pin_0
  N16: LED1.E, R6.Pin_0
  N17: LED1.DIG3, R8.Pin_0
  N18: LED1.APOS-A, R1.Pin_0
  N19: LED1.C, R2.Pin_1
  N20: LED1.A, R3.Pin_1
