# Fritzing sketch Automatic Light Source Tracking (saved by Fritzing 0.8.7b)

parts:
  元件1 = Arduino Uno (Rev3) - ICSP
  R1 = Resistor [tolerance=±5% resistance=220 package=THT]
  R2 = Photocell (LDR) [package=THT]
  J1 = Basic Servo

nets:
  N1: 元件1.A0, R1.Pin_0, R2.pin_1
  5V: 元件1.5V, R2.pin_0, J1.vcc
  N2: 元件1.D9_PWM, J1.pulse
  GND: 元件1.GND, R1.Pin_1, J1.gnd
