# Fritzing sketch back a car (saved by Fritzing 0.8.7b)
breadboards: 1

parts:
  U1 = HC-SR04 [chip_label=IC package="SIP (Single Inline) [THT]"]
  元件1 = Arduino Uno (Rev3) - ICSP
  U2 = LCD-16X2 [package=lcd-16x2]
  R1 = Rotary Potentiometer (Small) [maximum_resistance=100kΩ package=THT]
  J1 = Piezo Speaker

nets:
  VCC: U1.Vcc, 元件1.5V, U2.VDD
  N1: U1.Trig, 元件1.D2
  N2: U1.Echo, 元件1.D3_PWM
  GND: U1.GND, 元件1.GND, U2.VSS, U2.R_W, U2.K, R1.leg2, J1.pin1
  N3: 元件1.D8, U2.E
  N4: 元件1.D9_PWM, U2.DB4
  N5: 元件1.D10_PWM/SS, U2.DB5
  N6: 元件1.D11_PWM/MOSI, U2.DB6
  N7: 元件1.D12/MISO, U2.DB7
  N8: 元件1.D6_PWM, J1.pin2
  N9: 元件1.D7, U2.RS
  N10: 元件1.3V3, U2.A
  N11: U2.VO, R1.wiper

custom parts:
  HC-SR04: HC-SR04 ultrasound distance sensor
