# Fritzing sketch Stepper Motor driver (saved by Fritzing 0.8.7b)
breadboards: 1

parts:
  module1 = Step Motor
  R1 = Rotary Potentiometer (Small) [maximum_resistance=100kΩ package=THT]
  U1 = Stepper Motor Driver-v1.0 [package="DIP28 [THT]"]
  元件1 = Arduino Uno (Rev3) - ICSP

nets:
  N1: module1.yellow, U1.OUT3
  N2: module1.orange, U1.OUT4
  N3: module1.red, U1.COM
  N4: module1.pink, U1.OUT2
  N5: module1.blue, U1.OUT1
  N6: R1.leg1, U1.-, 元件1.GND
  N7: R1.wiper, 元件1.A0
  N8: R1.leg2, U1.+, 元件1.5V
  N9: U1.IN1, 元件1.D2
  N10: U1.IN2, 元件1.D4
  N11: U1.IN3, 元件1.D3_PWM
  N12: U1.IN4, 元件1.D5_PWM
  N13: U1.JD-VCC, U1.VCC

notes:
  Stepper Motor Driver

custom parts:
  Step Motor: step motor
  Stepper Motor Driver-v1.0: Stepper Motor Driver
